# Fritzing sketch OctoAlarmWiring (saved by Fritzing 1.0.1rc)
breadboards: 1

parts:
  Part1 = Arduino Nano (Rev3.0)
  J1 = Piezo Speaker
  Part2 = LED Tactile Button Breakout v10 [part_number=BOB-10467]

nets:
  N1: Part1.GND, J1.pin2, Part2.1, Part2.4
  N2: Part1.D2, J1.pin1
  N3: Part1.D10, Part2.2
  N4: Part1.D11/MOSI, Part2.3

notes:
  Version 1.0
